// Logisim project ALU.circ as structural Verilog: 1 circuit, main circuit main
module main (
  input  flood_carry,
  input  carry_in,
  input  or_enable,
  input  invert_a,
  input  invert_b,
  input  a0,
  input  b0,
  input  in_8,
  input  in_9,
  input  in_10,
  input  in_11,
  output out_12
);

  wire and_1_out, and_2_out, and_3_out, c0_out, c1_out, c2_out, g0_out, g1_out, g2_out, nor_1_out, nor_2_out,
       nor_3_out, p0_out, p1_out, p2_out, xor_1_out, xor_2_out, xor_3_out, xor_4_out, xor_5_out, xor_6_out,
       xor_8_out, xor_9_out;

  xor xor_1 (xor_1_out, a0, invert_a);
  xor xor_2 (xor_2_out, b0, invert_b);
  xor xor_3 (xor_3_out, in_8, invert_a);
  xor xor_4 (xor_4_out, in_9, invert_b);
  xor xor_5 (xor_5_out, in_10, invert_a);
  xor xor_6 (xor_6_out, in_11, invert_b);
  and g0 (g0_out, xor_1_out, ~or_enable, xor_2_out);  // AND_Gate
  or p0 (p0_out, xor_1_out, xor_2_out);
  and g1 (g1_out, xor_3_out, ~or_enable, xor_4_out);  // AND_Gate
  or p1 (p1_out, xor_3_out, xor_4_out);
  and g2 (g2_out, xor_5_out, ~or_enable, xor_6_out);  // AND_Gate
  or p2 (p2_out, xor_5_out, xor_6_out);
  nor nor_1 (nor_1_out, g0_out, ~p0_out);  // NOR_Gate
  nor nor_2 (nor_2_out, g1_out, ~p1_out);  // NOR_Gate
  nor nor_3 (nor_3_out, g2_out, ~p2_out);  // NOR_Gate
  xor xor_7 (out_12, c0_out, nor_1_out);
  xor xor_8 (xor_8_out, c1_out, nor_2_out);
  xor xor_9 (xor_9_out, c2_out, nor_3_out);
  or c0 (c0_out, carry_in, flood_carry);
  or c1 (c1_out, flood_carry, and_1_out, g0_out);
  or c2 (c2_out, flood_carry, and_2_out, and_3_out, g1_out);
  and and_1 (and_1_out, carry_in, p0_out);
  and and_2 (and_2_out, carry_in, p0_out, p1_out);
  and and_3 (and_3_out, g0_out, p1_out);
endmodule
